// Logisim project MIPS.circ as structural Verilog: 13 circuits, main circuit MIPS
module MIPS (
  input  clr,
  output [7:0] out_2,
  output [7:0] t4,
  output [7:0] t3,
  output [7:0] t2,
  output [7:0] t1,
  output [7:0] t0,
  output [7:0] sp_address,
  output [7:0] zero
);

  wire alu_encapsulated_1_branch_taken, and_1_out, and_2_out, clk_out, control_unit_1_alusrc,
       control_unit_1_beq, control_unit_1_bne, control_unit_1_jump, control_unit_1_memread,
       control_unit_1_memtoreg, control_unit_1_memwrite, control_unit_1_regdest, control_unit_1_regwrite,
       not_1_out, not_2_out, not_3_out, or_1_out;
  wire [2:0] control_unit_1_aluop;
  wire [3:0] instruction_memory_1_opcode__12_15, instruction_memory_1_src_reg_1__8_11,
       instruction_memory_1_src_reg_2__dst_reg_4_7, multiplexer_2_out;
  wire [7:0] adder_1_out, adder_2_out, alu_encapsulated_1_out_7, data_memory_1_memdata,
       instruction_memory_1_pc_read, multiplexer_1_out, multiplexer_3_out, multiplexer_4_out,
       multiplexer_5_out, multiplexer_6_out, multiplexer_7_out, register_file_1_read_data_1,
       register_file_1_read_data_2;

  not not_1 (not_1_out, clk_out);
  Adder adder_1 (.a(instruction_memory_1_pc_read), .b(8'h1), .out(adder_1_out));  // open: cin, cout
  Instruction_Memory instruction_memory_1 (
    .PC_write(multiplexer_5_out), .shamt(out_2[3:0]), .DstReg_Shamt_Addr_Immdt_0_3(out_2[7:4]),
    .Src_Reg_2__Dst_Reg_4_7(instruction_memory_1_src_reg_2__dst_reg_4_7),
    .Src_Reg_1__8_11(instruction_memory_1_src_reg_1__8_11),
    .Opcode__12_15(instruction_memory_1_opcode__12_15), .PC_read(instruction_memory_1_pc_read),
    .in_2(not_1_out));
  or or_1 (or_1_out, and_1_out, and_2_out);
  Adder adder_2 (.a(out_2), .b(adder_1_out), .out(adder_2_out));  // open: cin, cout
  and and_1 (and_1_out, control_unit_1_aluop[0], not_3_out, control_unit_1_aluop[2]);
  not not_2 (not_2_out, control_unit_1_aluop[0]);
  and and_2 (and_2_out, not_2_out, control_unit_1_aluop[2], control_unit_1_aluop[1]);
  Multiplexer #(.width(8)) multiplexer_1 (
    .in0(adder_1_out), .in1(adder_2_out), .out(multiplexer_1_out), .sel(alu_encapsulated_1_branch_taken));  // open: en
  Multiplexer #(.width(4)) multiplexer_2 (
    .in0(instruction_memory_1_src_reg_2__dst_reg_4_7), .in1(out_2[7:4]), .out(multiplexer_2_out),
    .sel(control_unit_1_regdest));  // open: en
  not not_3 (not_3_out, control_unit_1_aluop[1]);
  Clock clk (.out(clk_out));
  Control_Unit control_unit_1 (
    .OpCode(instruction_memory_1_opcode__12_15), .Jump(control_unit_1_jump),
    .RegDest(control_unit_1_regdest), .RegWrite(control_unit_1_regwrite), .MemRead(control_unit_1_memread),
    .MemWrite(control_unit_1_memwrite), .MemToReg(control_unit_1_memtoreg), .beq(control_unit_1_beq),
    .bne(control_unit_1_bne), .ALUsrc(control_unit_1_alusrc), .ALUop(control_unit_1_aluop));
  Register_file register_file_1 (
    .ReadReg1(instruction_memory_1_src_reg_1__8_11), .ReadReg2(instruction_memory_1_src_reg_2__dst_reg_4_7),
    .write_data(multiplexer_7_out), .Write_Reg_Address(multiplexer_2_out),
    .RegWrite(control_unit_1_regwrite), .Read_Data_1(register_file_1_read_data_1),
    .Read_Data_2(register_file_1_read_data_2), .zero(zero), .t0(t0), .t1(t1), .t2(t2), .t3(t3), .t4(t4),
    .sp(sp_address), .in_7(not_1_out), .clear(clr));
  Multiplexer #(.width(8)) multiplexer_3 (
    .in0(register_file_1_read_data_2), .in1(out_2), .out(multiplexer_3_out), .sel(control_unit_1_alusrc));  // open: en
  Multiplexer #(.width(8)) multiplexer_4 (
    .in0(register_file_1_read_data_1), .in1({4'b0000, out_2[3:0]}), .out(multiplexer_4_out), .sel(or_1_out));  // open: en
  Multiplexer #(.width(8)) multiplexer_5 (
    .in0(multiplexer_1_out),
    .in1({instruction_memory_1_src_reg_1__8_11, instruction_memory_1_src_reg_2__dst_reg_4_7}),
    .out(multiplexer_5_out), .sel(control_unit_1_jump));  // open: en
  Multiplexer #(.width(8)) multiplexer_6 (
    .in0(multiplexer_3_out), .in1(register_file_1_read_data_1), .out(multiplexer_6_out), .sel(or_1_out));  // open: en
  ALU_encapsulated alu_encapsulated_1 (
    .beq(control_unit_1_beq), .bne(control_unit_1_bne), .Data2(multiplexer_6_out),
    .ALUop(control_unit_1_aluop), .Branch_taken(alu_encapsulated_1_branch_taken),
    .out_7(alu_encapsulated_1_out_7), .Data1(multiplexer_4_out));
  Data_Memory data_memory_1 (
    .Address(alu_encapsulated_1_out_7), .Write_Data(register_file_1_read_data_2),
    .MemWrite(control_unit_1_memwrite), .MemRead(control_unit_1_memread), .MemData(data_memory_1_memdata),
    .clock(not_1_out));
  Multiplexer #(.width(8)) multiplexer_7 (
    .in0(alu_encapsulated_1_out_7), .in1(data_memory_1_memdata), .out(multiplexer_7_out),
    .sel(control_unit_1_memtoreg));  // open: en
endmodule

module ALU_encapsulated (
  input  beq,
  input  bne,
  input  [7:0] Data1,
  input  [7:0] Data2,
  input  [2:0] ALUop,
  output Branch_taken,
  output [7:0] out_7
);

  wire alu_8_by_art_1_p4, n7408_1_p3, n7408_1_p6, not_1_out;

  // ALU_8_by_ART alu_8_by_art_1: pin names not known; wires that end beside it: Data1, Data2, ALUop, alu_8_by_art_1_p4, out_7
  or or_1 (Branch_taken, n7408_1_p3, n7408_1_p6);
  not not_1 (not_1_out, alu_8_by_art_1_p4);
  // _7408 7408_1: pin names not known; wires that end beside it: beq, alu_8_by_art_1_p4, n7408_1_p3, bne, not_1_out, n7408_1_p6
endmodule

module Control_Unit (
  input  [3:0] OpCode,
  output Jump,
  output RegDest,
  output RegWrite,
  output MemRead,
  output MemWrite,
  output MemToReg,
  output beq,
  output bne,
  output ALUsrc,
  output [2:0] ALUop
);

  ROM #(.addrWidth(4), .dataWidth(12)) rom_1 (
    .addr(OpCode), .data({ALUop, ALUsrc, bne, beq, MemToReg, MemWrite, MemRead, RegWrite, RegDest, Jump}));  // open: sel

  // Notes on the sheet:
  //   contents of rom_1 (hex, n*v repeats v):
  //   110 606 704 1 806 406 a04 12c 304 6 504 d04 240 206 104 280
endmodule

module Register (
  input  [7:0] in_t0,
  input  [7:0] in_t1,
  input  c0,
  input  c1,
  input  [7:0] in_t2,
  input  [7:0] in_t3,
  input  c2,
  input  c3,
  input  [7:0] in_t4,
  input  [7:0] in_zero,
  input  c4,
  input  c_zero,
  input  [7:0] in_sp,
  input  c_sp,
  input  clear,
  output [7:0] t0,
  output [7:0] t1,
  output [7:0] t2,
  output [7:0] t3,
  output [7:0] t4,
  output [7:0] zero,
  output [7:0] sp
);

  wire [7:0] n7474_21_p3;

  // _7474 7474_1: pin names not known; wires that end beside it: in_t0[0], c0, t0[0], 1'b1, in_t0[1], c0, t0[1]
  // _7474 7474_2: pin names not known; wires that end beside it: 1'b0, in_t0[2], c0, t0[2], 1'b0, 1'b1, in_t0[3], c0, t0[3]
  // _7474 7474_3: pin names not known; wires that end beside it: in_t0[4], c0, t0[4], 1'b1, in_t0[5], c0
  // _7474 7474_4: pin names not known; wires that end beside it: 1'b0, in_t0[6], c0, t0[6], 1'b0, t0[5], 1'b1, in_t0[7], c0, t0[7]
  // _7474 7474_5: pin names not known; wires that end beside it: in_t2[0], c2, t2[0], 1'b1, in_t2[1], c2
  // _7474 7474_6: pin names not known; wires that end beside it: 1'b0, in_t2[2], c2, t2[2], 1'b0, t2[1], 1'b1, in_t2[3], c2, t2[3]
  // _7474 7474_7: pin names not known; wires that end beside it: in_t2[4], c2, t2[4], 1'b1, in_t2[5], c2
  // _7474 7474_8: pin names not known; wires that end beside it: 1'b0, in_t2[6], c2, t2[6], 1'b0, t2[5], 1'b1, in_t2[7], c2, t2[7]
  // _7474 7474_9: pin names not known; wires that end beside it: in_t4[0], c4, t4[0], 1'b1, in_t4[1], c4, t4[1]
  // _7474 7474_10: pin names not known; wires that end beside it: 1'b0, in_t4[2], c4, t4[2], 1'b0, 1'b1, in_t4[3], c4, t4[3]
  // _7474 7474_11: pin names not known; wires that end beside it: in_t4[4], c4, t4[4], 1'b1, in_t4[5], c4, t4[5]
  // _7474 7474_12: pin names not known; wires that end beside it: 1'b0, in_t4[6], c4, t4[6], 1'b0, 1'b1, in_t4[7], c4, t4[7]
  // _7474 7474_13: pin names not known; wires that end beside it: in_t1[0], c1, t1[0], 1'b1, in_t1[1], c1
  // _7474 7474_14: pin names not known; wires that end beside it: 1'b0, in_t1[2], c1, t1[2], 1'b0, t1[1], 1'b1, in_t1[3], c1, t1[3]
  // _7474 7474_15: pin names not known; wires that end beside it: in_t1[4], c1, t1[4], 1'b1, in_t1[5], c1, t1[5]
  // _7474 7474_16: pin names not known; wires that end beside it: 1'b0, in_t1[6], c1, t1[6], 1'b0, 1'b1, in_t1[7], c1, t1[7]
  // _7474 7474_17: pin names not known; wires that end beside it: in_sp[4], c_sp, sp[4], 1'b1, in_sp[5], c_sp, sp[5]
  // _7474 7474_18: pin names not known; wires that end beside it: 1'b0, in_sp[6], c_sp, sp[6], 1'b0, 1'b1, in_sp[7], c_sp, sp[7]
  // _7474 7474_19: pin names not known; wires that end beside it: in_t3[4], c3, t3[4], 1'b1, in_t3[5], c3
  // _7474 7474_20: pin names not known; wires that end beside it: 1'b0, in_t3[6], c3, t3[6], 1'b0, t3[5], 1'b1, in_t3[7], c3, t3[7]
  // _7474 7474_21: pin names not known; wires that end beside it: in_zero[0], c_zero, n7474_21_p3[0], 1'b1, in_zero[1], c_zero, n7474_21_p3[1]
  // _7474 7474_22: pin names not known; wires that end beside it: 1'b0, in_zero[2], c_zero, n7474_21_p3[2], 1'b0, 1'b1, in_zero[3], c_zero, n7474_21_p3[3]
  // _7474 7474_23: pin names not known; wires that end beside it: in_zero[4], c_zero, n7474_21_p3[4], 1'b1, in_zero[5], c_zero, n7474_21_p3[5]
  // _7474 7474_24: pin names not known; wires that end beside it: 1'b0, in_zero[6], c_zero, n7474_21_p3[6], 1'b0, 1'b1, in_zero[7], c_zero, n7474_21_p3[7]
  // _7474 7474_25: pin names not known; wires that end beside it: in_sp[0], c_sp, sp[0], 1'b1, in_sp[1], c_sp, sp[1]
  // _7474 7474_26: pin names not known; wires that end beside it: 1'b0, in_sp[2], c_sp, sp[2], 1'b0, 1'b1, in_sp[3], c_sp, sp[3]
  // _7474 7474_27: pin names not known; wires that end beside it: in_t3[0], c3, t3[0], 1'b1, in_t3[1], c3, t3[1]
  // _7474 7474_28: pin names not known; wires that end beside it: 1'b0, in_t3[2], c3, t3[2], 1'b0, 1'b1, in_t3[3], c3, t3[3]

  assign zero = {8{1'b0}};
endmodule

module Register_file (
  input  [3:0] ReadReg1,
  input  [3:0] ReadReg2,
  input  [7:0] write_data,
  input  clear,
  input  [3:0] Write_Reg_Address,
  input  RegWrite,
  input  in_7,
  output [7:0] Read_Data_1,
  output [7:0] Read_Data_2,
  output [7:0] zero,
  output [7:0] t0,
  output [7:0] t1,
  output [7:0] t2,
  output [7:0] t3,
  output [7:0] t4,
  output [7:0] sp
);

  wire and_1_out, decoder_1_out1, decoder_1_out2, decoder_1_out3, decoder_1_out4, decoder_1_out5,
       decoder_1_out6, not_1_out;
  wire [2:0] multiplexer_1_out;

  not not_1 (not_1_out, in_7);
  Multiplexer #(.width(3), .enable("false")) multiplexer_1 (
    .in0(3'b000), .in1(Write_Reg_Address[2:0]), .out(multiplexer_1_out), .sel(and_1_out));
  and and_1 (and_1_out, RegWrite, not_1_out);
  Decoder #(.select(3)) decoder_1 (
    .out1(decoder_1_out1), .out2(decoder_1_out2), .out3(decoder_1_out3), .out4(decoder_1_out4),
    .out5(decoder_1_out5), .out6(decoder_1_out6), .sel(multiplexer_1_out));  // open: out0, out7, en
  Register register_1 (
    .in_t0(write_data), .in_t1(write_data), .c0(decoder_1_out1), .c1(decoder_1_out2), .in_t2(write_data),
    .in_t3(write_data), .c2(decoder_1_out3), .c3(decoder_1_out4), .in_t4(write_data), .in_zero(write_data),
    .c4(decoder_1_out5), .in_sp(write_data), .c_sp(decoder_1_out6), .clear(clear), .t0(t0), .t1(t1), .t2(t2),
    .t3(t3), .t4(t4), .zero(zero), .sp(sp));  // open: c_zero
  Multiplexer #(.select(3), .width(8), .enable("false")) multiplexer_2 (
    .in0(zero), .in1(t0), .in2(t1), .in3(t2), .in4(t3), .in5(t4), .in6(sp), .out(Read_Data_1),
    .sel(ReadReg1[2:0]));  // open: in7
  Multiplexer #(.select(3), .width(8), .enable("false")) multiplexer_3 (
    .in0(zero), .in1(t0), .in2(t1), .in3(t2), .in4(t3), .in5(t4), .in6(sp), .out(Read_Data_2),
    .sel(ReadReg2[2:0]));  // open: in7
endmodule

module Data_Memory (
  input  [7:0] Address,
  input  [7:0] Write_Data,
  input  MemWrite,
  input  MemRead,
  input  clock,
  output [7:0] MemData
);

  wire not_1_out;

  not not_1 (not_1_out, clock);
  RAM #(.bus("separate")) ram_1 (
    .addr(Address), .din(Write_Data), .data(MemData), .str(MemWrite), .clk(not_1_out), .ld(MemRead));  // open: sel, clr
endmodule

module Instruction_Memory (
  input  [7:0] PC_write,
  input  in_2,
  output [3:0] shamt,
  output [3:0] DstReg_Shamt_Addr_Immdt_0_3,
  output [3:0] Src_Reg_2__Dst_Reg_4_7,
  output [3:0] Src_Reg_1__8_11,
  output [3:0] Opcode__12_15,
  output [7:0] PC_read
);

  Register_8bit register_8bit_1 (.\input (PC_write), .in_2(in_2), .\output (PC_read));
  ROM #(.dataWidth(20)) rom_1 (
    .addr(PC_read),
    .data({Opcode__12_15, Src_Reg_1__8_11, Src_Reg_2__Dst_Reg_4_7, DstReg_Shamt_Addr_Immdt_0_3, shamt}),
    .sel(1'b1));

  // Notes on the sheet:
  //   contents of rom_1 (hex, n*v repeats v):
  //   e66ff e010a e0201 c210b e0202 c2109 e0201 e0301 e0502 92340 90320 90430 e5501 f15fb 31000 e0401 6400
  //   86601 b4104 6100 86601 61505 6500 86601 55a2 6500 86601 752a2 6200 86601 e2388 6300 86601 83481
  //   d4340 6400 86601 e0146 e0255 11230 6300 86601 234fe 6400 86601 e0480 e05aa 54520 6200 86601 a23ff
  //   6300 86601 33500
endmodule

module Register_8bit (
  input  [7:0] \input ,
  input  in_2,
  output [7:0] \output 
);

  // _7474 7474_1: pin names not known; wires that end beside it: \input [1], in_2, \output [1], 1'b1, \input [0], in_2
  // _7474 7474_2: pin names not known; wires that end beside it: 1'b0, \input [2], in_2, \output [2], 1'b0, \output [0], 1'b1, \input [3], in_2, \output [3]
  // _7474 7474_3: pin names not known; wires that end beside it: \input [4], in_2, \output [4], 1'b1, \input [5], in_2
  // _7474 7474_4: pin names not known; wires that end beside it: 1'b0, \input [6], in_2, \output [6], 1'b0, \output [5], 1'b1, \input [7], in_2, \output [7]
endmodule

module PR (
  input  [7:0] _8,
  input  [7:0] _8_2,
  input  [7:0] _8_3,
  input  [7:0] _8_4,
  input  [7:0] _8_5,
  input  [7:0] _8_new_1,
  input  [7:0] _8_new_2,
  input  _1,
  input  _1_2,
  input  _1_3,
  input  _1_4,
  input  _1_5,
  input  _1_6,
  input  _1_7,
  input  _1_8,
  input  _1_9,
  input  [2:0] _3,
  input  [3:0] _4,
  input  [3:0] _4_2,
  input  [3:0] _4_3,
  input  [3:0] _4_4,
  input  [3:0] _4_5,
  input  in_23,
  output [7:0] out_24,
  output [7:0] out_25,
  output [7:0] out_26,
  output [7:0] out_27,
  output [7:0] out_28,
  output [7:0] out_29,
  output [7:0] out_30,
  output out_31,
  output out_32,
  output out_33,
  output out_34,
  output out_35,
  output out_36,
  output out_37,
  output out_38,
  output out_39,
  output [2:0] out_40,
  output [3:0] out_41,
  output [3:0] out_42,
  output [3:0] out_43,
  output [3:0] out_44,
  output [3:0] out_45
);

  Register_part #(.trigger("falling")) register_1 (.D(_8), .Q(out_24), .clk(in_23));  // open: en, clr
  Register_part #(.trigger("falling")) register_2 (.D(_8_2), .Q(out_25), .clk(in_23));  // open: en, clr
  Register_part #(.trigger("falling")) register_3 (.D(_8_3), .Q(out_26), .clk(in_23));  // open: en, clr
  Register_part #(.trigger("falling")) register_4 (.D(_8_4), .Q(out_27), .clk(in_23));  // open: en, clr
  Register_part #(.trigger("falling")) register_5 (.D(_8_5), .Q(out_28), .clk(in_23));  // open: en, clr
  Register_part #(.trigger("falling")) register_6 (.D(_8_new_1), .Q(out_29), .clk(in_23));  // open: en, clr
  Register_part #(.trigger("falling")) register_7 (.D(_8_new_2), .Q(out_30), .clk(in_23));  // open: en, clr
  Register_part #(.width(1), .trigger("falling")) register_8 (.D(_1), .Q(out_31), .clk(in_23));  // open: en, clr
  Register_part #(.width(1), .trigger("falling")) register_9 (.D(_1_2), .Q(out_32), .clk(in_23));  // open: en, clr
  Register_part #(.width(1), .trigger("falling")) register_10 (.D(_1_3), .Q(out_33), .clk(in_23));  // open: en, clr
  Register_part #(.width(1), .trigger("falling")) register_11 (.D(_1_4), .Q(out_34), .clk(in_23));  // open: en, clr
  Register_part #(.width(1), .trigger("falling")) register_12 (.D(_1_5), .Q(out_35), .clk(in_23));  // open: en, clr
  Register_part #(.width(1), .trigger("falling")) register_13 (.D(_1_6), .Q(out_36), .clk(in_23));  // open: en, clr
  Register_part #(.width(1), .trigger("falling")) register_14 (.D(_1_7), .Q(out_37), .clk(in_23));  // open: en, clr
  Register_part #(.width(1), .trigger("falling")) register_15 (.D(_1_8), .Q(out_38), .clk(in_23));  // open: en, clr
  Register_part #(.width(1), .trigger("falling")) register_16 (.D(_1_9), .Q(out_39), .clk(in_23));  // open: en, clr
  Register_part #(.width(3), .trigger("falling")) register_17 (.D(_3), .Q(out_40), .clk(in_23));  // open: en, clr
  Register_part #(.width(4), .trigger("falling")) register_18 (.D(_4), .Q(out_41), .clk(in_23));  // open: en, clr
  Register_part #(.width(4), .trigger("falling")) register_19 (.D(_4_2), .Q(out_42), .clk(in_23));  // open: en, clr
  Register_part #(.width(4), .trigger("falling")) register_20 (.D(_4_3), .Q(out_43), .clk(in_23));  // open: en, clr
  Register_part #(.width(4), .trigger("falling")) register_21 (.D(_4_4), .Q(out_44), .clk(in_23));  // open: en, clr
  Register_part #(.width(4), .trigger("falling")) register_22 (.D(_4_5), .Q(out_45), .clk(in_23));  // open: en, clr
endmodule

module MIPS_pipelined (
  input  clear,
  output out_2,
  output out_3,
  output [7:0] t0,
  output [7:0] t1,
  output [7:0] t2,
  output [7:0] t3,
  output [7:0] t4,
  output [7:0] sp
);

  wire alu_encapsulated_1_branch_taken, and_1_out, and_2_out, clock_1_out, control_0_1_alusrc_2,
       control_0_1_beq_2, control_0_1_bne_2, control_0_1_jump_2, control_0_1_memread_2,
       control_0_1_memtoreg_2, control_0_1_memwrite_2, control_0_1_regdest_2, control_0_1_regwrite_2,
       control_unit_1_alusrc, control_unit_1_beq, control_unit_1_bne, control_unit_1_jump,
       control_unit_1_memread, control_unit_1_memtoreg, control_unit_1_memwrite, control_unit_1_regdest,
       control_unit_1_regwrite, EX_MEM_out_33, EX_MEM_out_34, EX_MEM_out_35, EX_MEM_out_36, EX_MEM_out_37,
       hazard_detection_unit_1_hazard, ID_EX_out_31, ID_EX_out_32, ID_EX_out_33, ID_EX_out_34, ID_EX_out_35,
       ID_EX_out_36, ID_EX_out_39, MEM_WB_p9, MEM_WB_p10, not_1_out, not_2_out, not_3_out, or_1_out;
  wire [1:0] forwarding_unit_fwda, forwarding_unit_fwdb;
  wire [2:0] control_0_1_aluop_2, control_unit_1_aluop, ID_EX_out_40;
  wire [3:0] EX_MEM_out_42, hazard_detection_unit_1_if_id_rs_2, hazard_detection_unit_1_if_id_rt_2,
       ID_EX_out_41, ID_EX_out_42, ID_EX_out_43, ID_EX_out_44, IF_ID_out_41, IF_ID_out_42, IF_ID_out_43,
       IF_ID_out_44, IF_ID_out_45, instruction_memory_1_dstreg_shamt_addr_immdt_0_3,
       instruction_memory_1_opcode__12_15, instruction_memory_1_shamt, instruction_memory_1_src_reg_1__8_11,
       instruction_memory_1_src_reg_2__dst_reg_4_7, MEM_WB_p11, multiplexer_2_out, multiplexer_3_out,
       multiplexer_11_out;
  wire [7:0] adder_1_out, adder_2_out, alu_encapsulated_1_out_7, data_memory_1_memdata, EX_MEM_out_26,
       EX_MEM_out_30, ID_EX_out_24, ID_EX_out_25, ID_EX_out_26, ID_EX_out_27, ID_EX_out_30, IF_ID_out_24,
       IF_ID_out_25, IF_ID_out_27, instruction_memory_1_pc_read, MEM_WB_p7, MEM_WB_p8, multiplexer_1_out,
       multiplexer_4_out, multiplexer_5_out, multiplexer_6_out, multiplexer_7_out, multiplexer_8_out,
       multiplexer_9_out, multiplexer_10_out, multiplexer_12_out, register_file_1_read_data_1,
       register_file_1_read_data_2, undriven;

  not not_1 (not_1_out, clock_1_out);
  Multiplexer #(.width(8)) multiplexer_1 (
    .in0(adder_1_out), .in1(instruction_memory_1_pc_read), .out(multiplexer_1_out),
    .sel(hazard_detection_unit_1_hazard));  // open: en
  Adder adder_1 (.a(instruction_memory_1_pc_read), .b(8'h1), .out(adder_1_out));  // open: cin, cout
  Multiplexer #(.width(4)) multiplexer_2 (
    .in0(instruction_memory_1_src_reg_2__dst_reg_4_7), .in1(hazard_detection_unit_1_if_id_rt_2),
    .out(multiplexer_2_out), .sel(hazard_detection_unit_1_hazard));  // open: en
  Instruction_Memory instruction_memory_1 (
    .PC_write(multiplexer_10_out), .shamt(instruction_memory_1_shamt),
    .DstReg_Shamt_Addr_Immdt_0_3(instruction_memory_1_dstreg_shamt_addr_immdt_0_3),
    .Src_Reg_2__Dst_Reg_4_7(instruction_memory_1_src_reg_2__dst_reg_4_7),
    .Src_Reg_1__8_11(instruction_memory_1_src_reg_1__8_11),
    .Opcode__12_15(instruction_memory_1_opcode__12_15), .PC_read(instruction_memory_1_pc_read),
    .in_2(not_1_out));
  Multiplexer #(.width(4)) multiplexer_3 (
    .in0(instruction_memory_1_src_reg_1__8_11), .in1(hazard_detection_unit_1_if_id_rs_2),
    .out(multiplexer_3_out), .sel(hazard_detection_unit_1_hazard));  // open: en
  Multiplexer #(.width(8)) multiplexer_4 (
    .in0(adder_1_out), .in1(adder_2_out), .out(multiplexer_4_out), .sel(EX_MEM_out_37));  // open: en
  or or_1 (or_1_out, and_2_out, and_1_out);
  and and_1 (and_1_out, not_2_out, ID_EX_out_40[2], ID_EX_out_40[1]);
  PR IF_ID (
    ._8({instruction_memory_1_dstreg_shamt_addr_immdt_0_3, instruction_memory_1_shamt}),
    ._8_2(multiplexer_1_out),
    ._8_4({instruction_memory_1_src_reg_1__8_11, instruction_memory_1_src_reg_2__dst_reg_4_7}),
    ._4(instruction_memory_1_shamt), .in_23(not_1_out), .out_24(IF_ID_out_24), .out_25(IF_ID_out_25),
    .out_27(IF_ID_out_27), .out_41(IF_ID_out_41), ._4_2(instruction_memory_1_dstreg_shamt_addr_immdt_0_3),
    .out_42(IF_ID_out_42), ._4_3(instruction_memory_1_src_reg_2__dst_reg_4_7), .out_43(IF_ID_out_43),
    ._4_4(multiplexer_3_out), .out_44(IF_ID_out_44), ._4_5(instruction_memory_1_opcode__12_15),
    .out_45(IF_ID_out_45));  // open: _8_3, _8_5, _1, _1_2, _1_3, _1_4, _1_5, _1_6, _1_7, _1_8, _1_9, _3, out_26, out_28, out_31, out_32, out_33, out_34, out_35, out_36, out_37, out_38, out_39, out_40, _8_new_1, out_29, _8_new_2, out_30
  and and_2 (and_2_out, ID_EX_out_40[0], not_3_out, ID_EX_out_40[2]);
  not not_2 (not_2_out, ID_EX_out_40[0]);
  not not_3 (not_3_out, ID_EX_out_40[1]);
  Hazard_detection_unit hazard_detection_unit_1 (
    .ID_EX_MemRead(ID_EX_out_34), .ID_EX_Rt(ID_EX_out_43), .IF_ID_Rs(instruction_memory_1_src_reg_1__8_11),
    .IF_ID_Rt(multiplexer_2_out), .IF_ID_Rs_2(hazard_detection_unit_1_if_id_rs_2),
    .IF_ID_Rt_2(hazard_detection_unit_1_if_id_rt_2), .Hazard(hazard_detection_unit_1_hazard));
  Control_Unit control_unit_1 (
    .OpCode(IF_ID_out_45), .Jump(control_unit_1_jump), .RegDest(control_unit_1_regdest),
    .RegWrite(control_unit_1_regwrite), .MemRead(control_unit_1_memread), .MemWrite(control_unit_1_memwrite),
    .MemToReg(control_unit_1_memtoreg), .beq(control_unit_1_beq), .bne(control_unit_1_bne),
    .ALUsrc(control_unit_1_alusrc), .ALUop(control_unit_1_aluop));
  Register_file register_file_1 (
    .ReadReg1(IF_ID_out_44), .ReadReg2(IF_ID_out_43), .write_data(multiplexer_12_out),
    .Write_Reg_Address(MEM_WB_p11), .RegWrite(MEM_WB_p9), .Read_Data_1(register_file_1_read_data_1),
    .Read_Data_2(register_file_1_read_data_2), .t0(t0), .t1(t1), .t2(t2), .t3(t3), .t4(t4), .sp(sp),
    .in_7(not_1_out), .clear(clear));  // open: zero
  Clock clock_1 (.out(clock_1_out));
  control_0 control_0_1 (
    .Jump(control_unit_1_jump), .RegDest(control_unit_1_regdest), .RegWrite(control_unit_1_regwrite),
    .MemRead(control_unit_1_memread), .MemWrite(control_unit_1_memwrite), .MemToReg(control_unit_1_memtoreg),
    .beq(control_unit_1_beq), .bne(control_unit_1_bne), .alusrc(control_unit_1_alusrc),
    .aluop(control_unit_1_aluop), .Hazard(hazard_detection_unit_1_hazard), .Jump_2(control_0_1_jump_2),
    .RegDest_2(control_0_1_regdest_2), .RegWrite_2(control_0_1_regwrite_2),
    .MemRead_2(control_0_1_memread_2), .MemWrite_2(control_0_1_memwrite_2),
    .MemToReg_2(control_0_1_memtoreg_2), .beq_2(control_0_1_beq_2), .bne_2(control_0_1_bne_2),
    .alusrc_2(control_0_1_alusrc_2), .aluop_2(control_0_1_aluop_2));
  PR ID_EX (
    ._8(IF_ID_out_24), ._8_2(register_file_1_read_data_1), ._8_3(register_file_1_read_data_2),
    ._8_4(IF_ID_out_25), ._1(control_0_1_jump_2), ._1_2(control_0_1_regdest_2),
    ._1_3(control_0_1_regwrite_2), ._1_4(control_0_1_memread_2), ._1_5(control_0_1_memwrite_2),
    ._1_6(control_0_1_memtoreg_2), ._1_7(control_0_1_beq_2), ._1_8(control_0_1_bne_2),
    ._1_9(control_0_1_alusrc_2), ._3(control_0_1_aluop_2), ._4(IF_ID_out_41), .in_23(not_1_out),
    .out_24(ID_EX_out_24), .out_25(ID_EX_out_25), .out_26(ID_EX_out_26), .out_27(ID_EX_out_27),
    .out_31(ID_EX_out_31), .out_32(ID_EX_out_32), .out_33(ID_EX_out_33), .out_34(ID_EX_out_34),
    .out_35(ID_EX_out_35), .out_36(ID_EX_out_36), .out_37(out_2), .out_38(out_3), .out_39(ID_EX_out_39),
    .out_40(ID_EX_out_40), .out_41(ID_EX_out_41), ._4_2(IF_ID_out_42), .out_42(ID_EX_out_42),
    ._4_3(IF_ID_out_43), .out_43(ID_EX_out_43), ._4_4(IF_ID_out_44), .out_44(ID_EX_out_44),
    ._8_new_2(IF_ID_out_27), .out_30(ID_EX_out_30));  // open: _8_5, out_28, _4_5, out_45, _8_new_1, out_29
  Forwarding_Unit forwarding_unit (
    .MEM_WB_RegWrite(MEM_WB_p9), .EX_MEM_RegWrite(EX_MEM_out_33), .MEM_WB_Rd(MEM_WB_p11),
    .EX_MEM_Rd(EX_MEM_out_42), .ID_EX_Rs(ID_EX_out_44), .ID_EX_Rt(ID_EX_out_43), .FwdA(forwarding_unit_fwda),
    .FwdB(forwarding_unit_fwdb));
  Multiplexer #(.select(2), .width(8)) multiplexer_5 (
    .in0(multiplexer_6_out), .in1(multiplexer_12_out), .in2(EX_MEM_out_30), .out(multiplexer_5_out),
    .sel(forwarding_unit_fwda));  // open: in3, en
  Multiplexer #(.width(8)) multiplexer_6 (
    .in0(ID_EX_out_25), .in1({4'b0000, ID_EX_out_41}), .out(multiplexer_6_out), .sel(or_1_out));  // open: en
  Adder adder_2 (.a(ID_EX_out_27), .b(ID_EX_out_24), .out(adder_2_out));  // open: cin, cout
  Multiplexer #(.select(2), .width(8)) multiplexer_7 (
    .in0(multiplexer_9_out), .in1(multiplexer_12_out), .in2(EX_MEM_out_30), .out(multiplexer_7_out),
    .sel(forwarding_unit_fwdb));  // open: in3, en
  Multiplexer #(.width(8)) multiplexer_8 (
    .in0(ID_EX_out_26), .in1({ID_EX_out_42, ID_EX_out_41}), .out(multiplexer_8_out), .sel(ID_EX_out_39));  // open: en
  Multiplexer #(.width(8)) multiplexer_9 (
    .in0(multiplexer_8_out), .in1(ID_EX_out_25), .out(multiplexer_9_out), .sel(or_1_out));  // open: en
  Multiplexer #(.width(8)) multiplexer_10 (
    .in0(multiplexer_4_out), .in1(undriven), .out(multiplexer_10_out), .sel(ID_EX_out_31));  // open: en
  ALU_encapsulated alu_encapsulated_1 (
    .beq(out_2), .bne(out_3), .Data2(multiplexer_7_out), .ALUop(ID_EX_out_40),
    .Branch_taken(alu_encapsulated_1_branch_taken), .out_7(alu_encapsulated_1_out_7),
    .Data1(multiplexer_5_out));
  Multiplexer #(.width(4)) multiplexer_11 (
    .in0(ID_EX_out_43), .in1(ID_EX_out_42), .out(multiplexer_11_out), .sel(ID_EX_out_32));  // open: en
  PR EX_MEM (
    ._8_3(ID_EX_out_26), ._1_3(ID_EX_out_33), ._1_4(ID_EX_out_34), ._1_5(ID_EX_out_35), ._1_6(ID_EX_out_36),
    ._1_7(alu_encapsulated_1_branch_taken), .in_23(not_1_out), .out_26(EX_MEM_out_26),
    .out_33(EX_MEM_out_33), .out_34(EX_MEM_out_34), .out_35(EX_MEM_out_35), .out_36(EX_MEM_out_36),
    .out_37(EX_MEM_out_37), ._4_2(multiplexer_11_out), .out_42(EX_MEM_out_42),
    ._8_new_2(alu_encapsulated_1_out_7), .out_30(EX_MEM_out_30));  // open: _8, _8_2, _8_4, _8_5, _1, _1_2, _1_8, _1_9, _3, _4, out_24, out_25, out_27, out_28, out_31, out_32, out_38, out_39, out_40, out_41, _4_3, out_43, _4_4, out_44, _4_5, out_45, _8_new_1, out_29
  Data_Memory data_memory_1 (
    .Address(EX_MEM_out_30), .Write_Data(EX_MEM_out_26), .MemWrite(EX_MEM_out_35), .MemRead(EX_MEM_out_34),
    .MemData(data_memory_1_memdata), .clock(not_1_out));
  // PR MEM_WB: pin names not known; wires that end beside it: EX_MEM_out_30, data_memory_1_memdata, EX_MEM_out_33, EX_MEM_out_36, EX_MEM_out_42, not_1_out, MEM_WB_p7, MEM_WB_p8, MEM_WB_p9, MEM_WB_p10, MEM_WB_p11
  Multiplexer #(.width(8)) multiplexer_12 (
    .in0(MEM_WB_p7), .in1(MEM_WB_p8), .out(multiplexer_12_out), .sel(MEM_WB_p10));  // open: en

  // Notes on the sheet:
  //   RD, RT,RS
  //   A
  //   B
endmodule

module Forwarding_Unit (
  input  MEM_WB_RegWrite,
  input  EX_MEM_RegWrite,
  input  [3:0] MEM_WB_Rd,
  input  [3:0] EX_MEM_Rd,
  input  [3:0] ID_EX_Rs,
  input  [3:0] ID_EX_Rt,
  output [1:0] FwdA,
  output [1:0] FwdB
);

  wire and_1_out, and_2_out, comparator_1_eq, comparator_2_eq, comparator_3_eq, comparator_4_eq,
       comparator_5_eq, comparator_6_eq, not_1_out, not_2_out, not_3_out, not_4_out;
  wire [1:0] and_4_out, and_6_out;

  Comparator #(.width(4)) comparator_1 (.a(MEM_WB_Rd), .b(4'b0000), .eq(comparator_1_eq));  // open: gt, lt
  Comparator #(.width(4)) comparator_2 (.a(EX_MEM_Rd), .b(4'b0000), .eq(comparator_2_eq));  // open: gt, lt
  Comparator #(.width(4)) comparator_3 (.a(ID_EX_Rs), .b(EX_MEM_Rd), .eq(comparator_3_eq));  // open: gt, lt
  Comparator #(.width(4)) comparator_4 (.a(ID_EX_Rt), .b(EX_MEM_Rd), .eq(comparator_4_eq));  // open: gt, lt
  Comparator #(.width(4)) comparator_5 (.a(MEM_WB_Rd), .b(ID_EX_Rt), .eq(comparator_5_eq));  // open: gt, lt
  not not_1 (not_1_out, comparator_1_eq);
  not not_2 (not_2_out, comparator_2_eq);
  Comparator #(.width(4)) comparator_6 (.a(MEM_WB_Rd), .b(ID_EX_Rs), .eq(comparator_6_eq));  // open: gt, lt
  and and_1 (and_1_out, EX_MEM_RegWrite, not_2_out, comparator_3_eq);
  not not_3 (not_3_out, and_1_out);
  and and_2 (and_2_out, EX_MEM_RegWrite, not_2_out);
  and and_3 (and_6_out[1], not_2_out, EX_MEM_RegWrite, comparator_4_eq);
  and and_4 (and_4_out[0], MEM_WB_RegWrite, not_1_out, not_3_out, comparator_6_eq);
  not not_4 (not_4_out, and_6_out[1]);
  and and_5 (and_4_out[1], and_2_out, comparator_3_eq);
  and and_6 (and_6_out[0], not_4_out, MEM_WB_RegWrite, not_1_out, comparator_5_eq);
  Multiplexer #(.select(2), .width(2)) multiplexer_1 (
    .in0(2'b00), .in1(2'b01), .in2(2'b10), .in3(2'b00), .out(FwdA), .sel(and_4_out));  // open: en
  Multiplexer #(.select(2), .width(2)) multiplexer_2 (
    .in0(2'b00), .in1(2'b01), .in2(2'b10), .in3(2'b00), .out(FwdB), .sel(and_6_out));  // open: en

  // Notes on the sheet:
  //   Forward A = 01
  //   Forward A = 10
  //   Forward B = 01
  //   Forward B = 10
endmodule

module Hazard_detection_unit (
  input  ID_EX_MemRead,
  input  [3:0] ID_EX_Rt,
  input  [3:0] IF_ID_Rs,
  input  [3:0] IF_ID_Rt,
  output [3:0] IF_ID_Rs_2,
  output [3:0] IF_ID_Rt_2,
  output Hazard
);

  wire comparator_1_eq, comparator_2_eq, or_1_out;

  Comparator #(.width(4)) comparator_1 (.a(ID_EX_Rt), .b(IF_ID_Rs), .eq(comparator_1_eq));  // open: gt, lt
  Comparator #(.width(4)) comparator_2 (.a(ID_EX_Rt), .b(IF_ID_Rt), .eq(comparator_2_eq));  // open: gt, lt
  or or_1 (or_1_out, comparator_1_eq, comparator_2_eq);
  and and_1 (Hazard, ID_EX_MemRead, or_1_out);

  assign IF_ID_Rs_2 = IF_ID_Rs;
  assign IF_ID_Rt_2 = IF_ID_Rt;
endmodule

module control_0 (
  input  Jump,
  input  RegDest,
  input  RegWrite,
  input  MemRead,
  input  MemWrite,
  input  MemToReg,
  input  beq,
  input  bne,
  input  alusrc,
  input  [2:0] aluop,
  input  Hazard,
  output Jump_2,
  output RegDest_2,
  output RegWrite_2,
  output MemRead_2,
  output MemWrite_2,
  output MemToReg_2,
  output beq_2,
  output bne_2,
  output alusrc_2,
  output [2:0] aluop_2
);

  Multiplexer multiplexer_1 (.in0(Jump), .in1(1'b0), .out(Jump_2), .sel(Hazard));  // open: en
  Multiplexer multiplexer_2 (.in0(RegDest), .in1(1'b0), .out(RegDest_2), .sel(Hazard));  // open: en
  Multiplexer multiplexer_3 (.in0(RegWrite), .in1(1'b0), .out(RegWrite_2), .sel(Hazard));  // open: en
  Multiplexer multiplexer_4 (.in0(MemRead), .in1(1'b0), .out(MemRead_2), .sel(Hazard));  // open: en
  Multiplexer multiplexer_5 (.in0(MemWrite), .in1(1'b0), .out(MemWrite_2), .sel(Hazard));  // open: en
  Multiplexer multiplexer_6 (.in0(MemToReg), .in1(1'b0), .out(MemToReg_2), .sel(Hazard));  // open: en
  Multiplexer multiplexer_7 (.in0(beq), .in1(1'b0), .out(beq_2), .sel(Hazard));  // open: en
  Multiplexer multiplexer_8 (.in0(bne), .in1(1'b0), .out(bne_2), .sel(Hazard));  // open: en
  Multiplexer multiplexer_9 (.in0(alusrc), .in1(1'b0), .out(alusrc_2), .sel(Hazard));  // open: en
  Multiplexer #(.width(3)) multiplexer_10 (.in0(aluop), .in1(3'b000), .out(aluop_2), .sel(Hazard));  // open: en
endmodule
